# Fritzing sketch Exam project (saved by Fritzing 1.0.6)
breadboards: 1

parts:
  Part1 = Arduino Uno (Rev3) - ICSP
  Q1 = NPN-Transistor [package="TO92 [THT]"]
  V3 = DC Power [voltage=9V internal_resistance=0.1Ω]
  R1 = Resistor [tolerance=±5% power=0.25W resistance=10 package=THT]
  R3 = Resistor [tolerance=±5% power=0.25W resistance=10k package=THT]
  S1 = Tilt Switch [package=THT]
  L1 = Solenoid
  M2 = Stepper Motor - Bipolar
  U2 = LCD-16X2 [package=lcd-8x2]
  Q2 = NPN-Transistor [package="TO92 [THT]"]
  R4 = Resistor [tolerance=±5% power=0.25W resistance=10 package=THT]
  Q3 = NPN-Transistor [package="TO92 [THT]"]
  Q4 = NPN-Transistor [package="TO92 [THT]"]
  R5 = Resistor [tolerance=±5% power=0.25W resistance=10 package=THT]
  R6 = Resistor [tolerance=±5% power=0.25W resistance=10 package=THT]
  M3 = Stepper Motor - Bipolar
  S2 = Hall Sensor [part_number=WSH130 package=TO92]
  S3 = Hall Sensor [part_number=WSH130 package=TO92]
  R7 = Rotary Potentiometer (Small) [maximum_resistance=10kΩ knob_status=50% power=0.5W package=THT]
  D1 = Rectifier Diode [part_number=1N4001 package="300 mil [THT]"]
  Q5 = NPN-Transistor [package="TO92 [THT]"]
  R8 = Resistor [tolerance=±5% power=0.25W resistance=10 package=THT]
  R9 = Resistor [tolerance=±5% power=0.25W resistance=10k package=THT]
  R10 = Resistor [tolerance=±5% power=0.25W resistance=10k package=THT]

nets:
  N1: Part1.A3, S2.OUT, R9.Pin_1
  N2: Part1.A4/SDA, S3.OUT, R10.Pin_1
  N3: Part1.A5/SCL, R3.Pin_0, S1.Pin_2
  Arduino 5V: Part1.5V, S1.Pin_1, U2.VDD, U2.A, S2.VCC, S3.VCC, R7.leg2, R9.Pin_0, R10.Pin_0
  GND: Part1.GND, Q1.E, V3.V-, R3.Pin_1, U2.VSS, U2.R_W, U2.K, Q2.E, Q3.E, Q4.E, S2.GND, S3.GND, R7.leg1, Q5.E
  N4: Part1.D9_PWM, R8.Pin_0
  N5: Part1.D10_PWM/SS, R5.Pin_0
  N6: Part1.D11_PWM/MOSI, R6.Pin_0
  N7: Part1.D12/MISO, R4.Pin_0
  N8: Part1.D13/SCK, R1.Pin_0
  LCD RS: Part1.D2, U2.RS
  N9: Part1.D3_PWM, U2.E
  N10: Part1.D4, U2.DB4
  N11: Part1.D5_PWM, U2.DB5
  N12: Part1.D6_PWM, U2.DB6
  N13: Part1.D7, U2.DB7
  9V: Part1.VIN, V3.V+, L1.pin1, M2.A, M2.B, M3.A, M3.B, D1.cathode
  N14: Q1.B, R1.Pin_1
  N15: Q1.C, M2.D
  N16: L1.pin2, D1.anode, Q5.C
  N17: M2.C, Q2.C
  N18: U2.VO, R7.wiper
  N19: Q2.B, R4.Pin_1
  N20: Q3.B, R5.Pin_1
  N21: Q3.C, M3.C
  N22: Q4.B, R6.Pin_1
  N23: Q4.C, M3.D
  N24: Q5.B, R8.Pin_1

custom parts:
  Hall Sensor: A Hall Sensor
